# Fritzing sketch Morse trainer breadbord only (saved by Fritzing 0.9.2b)
circuit board: 6.42cm x 4.8cm
breadboards: 1

parts:
  R1 = Trimmer Potentiometer [maximum_resistance=10kΩ package=THT]
  Pro_mini = Arduino Pro Mini v13
  S1 = Pushbutton [package="[THT]"]
  S3 = SPST Switch [package=switch-spdt_lock.007s]
  J2 = female pin header, 4 pins [form="♀ (female)"]
  J3 = female pin header, 1 pin [form="♀ (female)"]
  J4 = female pin header, 1 pin [form="♀ (female)"]
  J5 = male pin header, 3 pins [form="♂ (male)"]
  Grove1 = Grove OLED 128x96  # not connected

nets:
  N1: R1.leg1, Pro_mini.GND, Pro_mini.D2, S1.Pin_1, S1.Pin_2, S1.Pin_3, S1.Pin_4, J2.pin1
  N2: R1.wiper, Pro_mini.A0
  N3: R1.leg2, Pro_mini.VCC, S3.S, J2.pin2
  N4: S3.P, J5.pin3
  N5: J2.pin3, J4.pin1
  N6: J2.pin4, J3.pin1

notes:
  jmp
  A  B  C  D  E  F  G  H  I  J  K  L  M  N  O  P  Q  R  S  T  U  V  W  X
  01 02 03 04 05 06 07 08 09 10 11 12 13 14 15 16 17 18
  + -
  Trainer
  HV 1.0
  Morse
  gnd A4 A5 A6 A7
  Off On
  To A4
  To A5
  NC - +
  PCB incomplete see separate file
  Scheme invalid

custom parts:
  Arduino Pro Mini v13: It's blue! It's thin! It's the Arduino Pro Mini! SparkFun's minimal design approach to Arduino. This is a 5V Arduino running the 16MHz bootloader. Arduino Pro Mini does not come with connectors populated so that you can solder in any connector or wire with any orientation you need. We recommend first time Arduino users start with the Uno R3. It's a great board that will get you up and running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
